# Fritzing sketch board (saved by Fritzing 0.8.7b)
breadboards: 1

parts:
  J1 = Basic Servo
  U1 = Voltage Regulator - 5V [package="TO220 [THT]"]
  Bauteil1 = Arduino Leonardo (Rev3b)
  J2 = Screw terminal - 2 pins [part_number=Power package=THT]
  C2 = Electrolytic Capacitor [capacitance=100nF voltage=20V part_number=330nF package="100 mil [THT, electrolytic]"]
  JP3 = Header 10 [part_number="RN-171, P 1-10" package=1x10-2mm-smd]
  JP1 = Header 10 [part_number="RN-171, P11-20" package=1x10-2mm-smd]  # not connected
  Bauteil4 = Tri-Axis Gyro Breakout - L3G4200D [part_number=Gyro-Sensor]
  Pololu_A1 = Pololu A4988 [package=SO16]
  Pololu_A2 = Pololu A4988 [package=SO16]
  C3 = Electrolytic Capacitor [capacitance=47µF voltage=16V part_number=100uF package="100 mil [THT, electrolytic]"]
  J7 = screw terminal, 4 pins
  C4 = Ceramic Capacitor [capacitance=100nF voltage=35V package="100 mil [THT, multilayer]"]
  J11 = screw terminal, 4 pins
  C5 = Electrolytic Capacitor [capacitance=47µF voltage=16V part_number=100uF package="100 mil [THT, electrolytic]"]
  J12 = Infrared Proximity Sensor
  J13 = double row male pin header, 6 pins [form="♂ (male)" part_number=MS1-3/1]
  J3 = male pin header, 3 pins [form="♂ (male)" part_number=MB1030]
  J14 = male pin header, 3 pins [form="♂ (male)" part_number=Servo]
  J15 = double row male pin header, 6 pins [form="♂ (male)" part_number=MS1-3/2]
  J16 = male pin header, 4 pins [form="♂ (male)" part_number=MPU6050]
  V1 = DC Power [voltage=12V]

nets:
  GND: J1.gnd, U1.GND, Bauteil1.GND, J2.pin1, C2.-, JP3.1, Bauteil4.GND, Pololu_A1.GND, Pololu_A2.GND, C3.-, C4.0, C5.-, J12.GND, J13.pin4, J13.pin5, J13.pin6, J3.pin2, J14.pin1, J15.pin4, J15.pin5, J15.pin6, J16.pin2, V1.V-
  VCC: J1.vcc, U1.output_voltage, Bauteil4.VCC, C4.1, J12.Vcc, J3.pin3, J14.pin2, J16.pin1
  N1: J1.pulse, Bauteil1.D5_PWM, J14.pin3
  N2: U1.input_voltage, Bauteil1.VIN, J2.pin2, C2.+, Pololu_A1.VMOT, Pololu_A2.VMOT, C3.+, C5.+, V1.V+
  N3: Bauteil1.D0/RX, JP3.9
  N4: Bauteil1.D1/TX, JP3.8
  N5: Bauteil1.D4/A6, Pololu_A1.ENABLE, Pololu_A2.ENABLE
  N6: Bauteil1.D6_PWM/A7, Pololu_A2.STEP
  N7: Bauteil1.3V3, JP3.10
  VDD: Bauteil1.5V, Pololu_A1.VDD, Pololu_A2.VDD
  N8: Bauteil1.A0, J12.Vout, J3.pin1
  N9: Bauteil1.D8/A8, Pololu_A2.DIR
  N10: Bauteil1.D12/A11, Pololu_A1.STEP
  N11: Bauteil1.D13_PWM, Pololu_A1.DIR
  N12: Bauteil1.SDA, Bauteil4.SDA, J16.pin4
  N13: Bauteil1.SCL, Bauteil4.SCL, J16.pin3
  N14: Pololu_A1.MS1, J15.pin1
  N15: Pololu_A1.MS2, J15.pin2
  N16: Pololu_A1.MS3, J15.pin3
  N17: Pololu_A1.RESET, Pololu_A1.SLEEP
  N18: Pololu_A1.1B, J11.pin4
  N19: Pololu_A1.1A, J11.pin3
  N20: Pololu_A1.2A, J11.pin2
  N21: Pololu_A1.2B, J11.pin1
  N22: Pololu_A2.MS1, J13.pin1
  N23: Pololu_A2.MS2, J13.pin2
  N24: Pololu_A2.MS3, J13.pin3
  N25: Pololu_A2.RESET, Pololu_A2.SLEEP
  N26: Pololu_A2.1B, J7.pin4
  N27: Pololu_A2.1A, J7.pin3
  N28: Pololu_A2.2A, J7.pin2
  N29: Pololu_A2.2B, J7.pin1

notes:
  RN-171
