# Fritzing sketch board_magbot (saved by Fritzing 0.8.7b)
circuit board: 7.9cm x 5.5cm
breadboards: 1

parts:
  J1 = Basic Servo [part_number=Servo]
  U1 = Voltage Regulator - 5V [package="TO220 [THT]"]
  Bauteil1 = Arduino Leonardo (Rev3b)
  C2 = Electrolytic Capacitor [capacitance=100nF voltage=20V part_number=330nF package="100 mil [THT, electrolytic]"]
  JP3 = Header 10 [part_number="RN-171, P 1-10" package=1x10-2mm-smd]
  JP1 = Header 10 [part_number="RN-171, P11-20" package=1x10-2mm-smd]  # not connected
  Bauteil4 = Tri-Axis Gyro Breakout - L3G4200D [part_number=Gyro-Sensor]
  Pololu_A2 = Pololu A4988 [part_number=Stepper1 package=SO16]
  C3 = Electrolytic Capacitor [capacitance=47µF voltage=16V part_number=100uF package="100 mil [THT, electrolytic]"]
  C4 = Ceramic Capacitor [capacitance=100nF voltage=35V package="100 mil [THT, multilayer]"]
  C5 = Electrolytic Capacitor [capacitance=47µF voltage=16V part_number=100uF package="100 mil [THT, electrolytic]"]
  J12 = Infrared Proximity Sensor [part_number=MB1030]
  J13 = double row male pin header, 6 pins [form="♂ (male)" part_number=MS1-3/1]
  J15 = double row male pin header, 6 pins [form="♂ (male)" part_number=MS1-3/2]
  J16 = male pin header, 4 pins [form="♂ (male)" part_number=MPU6050]
  V1 = DC Power [voltage=12V]
  D1 = Rectifier Diode [part_number=DO-201AD package="300 mil [THT]"]
  R1 = Resistor [tolerance=±5% resistance=47k package=THT]
  R2 = Resistor [tolerance=±5% resistance=33k package=THT]
  Pololu_A1 = Pololu A4988 [package=SO16]
  J17 = double row male pin header, 2 pins [form="♂ (male)"]
  J11 = screw terminal, 4 pins
  J2 = screw terminal, 2 pins
  J7 = screw terminal, 4 pins

nets:
  GND: J1.gnd, U1.GND, Bauteil1.GND, C2.-, JP3.1, Bauteil4.GND, Pololu_A2.GND, C3.-, C4.0, C5.-, J12.GND, J13.pin4, J13.pin5, J13.pin6, J15.pin4, J15.pin5, J15.pin6, J16.pin2, V1.V-, R2.Pin_1, Pololu_A1.GND, J17.pin1, J2.pin1
  VCC: J1.vcc, U1.output_voltage, Bauteil4.VCC, C4.1, J12.Vcc, J16.pin1, J17.pin2
  N1: J1.pulse, Bauteil1.D5_PWM
  N2: U1.input_voltage, Bauteil1.VIN, C2.+, Pololu_A2.VMOT, C3.+, C5.+, D1.cathode, R1.Pin_1, Pololu_A1.VMOT
  N3: Bauteil1.D0/RX, JP3.9
  N4: Bauteil1.D1/TX, JP3.8
  N5: Bauteil1.D3_PWM/SCL, Bauteil1.SCL, Bauteil4.SCL, J16.pin3
  N6: Bauteil1.D4/A6, Pololu_A2.ENABLE, Pololu_A1.ENABLE
  N7: Bauteil1.D6_PWM/A7, Pololu_A2.STEP
  N8: Bauteil1.3V3, JP3.10
  VDD: Bauteil1.5V, Pololu_A2.VDD, Pololu_A1.VDD
  N9: Bauteil1.A0, J12.Vout
  N10: Bauteil1.A5, R1.Pin_0, R2.Pin_0
  N11: Bauteil1.D8/A8, Pololu_A2.DIR
  N12: Bauteil1.D12/A11, Pololu_A1.STEP
  N13: Bauteil1.D13_PWM, Pololu_A1.DIR
  N14: Bauteil1.SDA, Bauteil4.SDA, J16.pin4
  N15: Pololu_A2.MS1, J13.pin1
  N16: Pololu_A2.MS2, J13.pin2
  N17: Pololu_A2.MS3, J13.pin3
  N18: Pololu_A2.RESET, Pololu_A2.SLEEP
  N19: Pololu_A2.1B, J7.pin4
  N20: Pololu_A2.1A, J7.pin3
  N21: Pololu_A2.2A, J7.pin2
  N22: Pololu_A2.2B, J7.pin1
  N23: J15.pin1, Pololu_A1.MS1
  N24: J15.pin2, Pololu_A1.MS2
  N25: J15.pin3, Pololu_A1.MS3
  N26: V1.V+, D1.anode, J2.pin2
  N27: Pololu_A1.RESET, Pololu_A1.SLEEP
  N28: Pololu_A1.1B, J11.pin4
  N29: Pololu_A1.1A, J11.pin3
  N30: Pololu_A1.2A, J11.pin2
  N31: Pololu_A1.2B, J11.pin1

notes:
  RN-171
  Servo
  Projekt: Magbot
  MB1030
  MPU6050
  5V
  VIN
  3,3V
  GND
  A0
  SCL
  SDA
  D5
  MS1
  Magbot 1.0
  Stepper 1
  Stepper 2
  Motor 2
  Motor 1
  -
  --
  33k
  47k
  100uF
  0.33uF
  100nF
  7805
  MS3*
